# Fritzing sketch Sketch for Castle (saved by Fritzing 0.9.3b)
breadboards: 1

parts:
  Part1 = PocketBeagle
  R1 = Resistor [tolerance=±5% resistance=220 package="2010 [SMD]"]
  R2 = Resistor [tolerance=±5% resistance=220 package="2010 [SMD]"]
  R3 = Resistor [tolerance=±5% resistance=220 package="2010 [SMD]"]
  LED1 = smd LED [color="Blue (430nm)" package="0603 [SMD]"]
  LED2 = smd LED [color="Green (555nm)" package="0603 [SMD]"]
  LED3 = smd LED [color="Red (633nm)" package="0603 [SMD]"]

nets:
  N1: Part1.AIN6/GPIO87, R2.Pin_1
  N2: Part1.GPIO89, R3.Pin_1
  N3: Part1.GND, LED1.cathode, LED2.cathode, LED3.cathode
  N4: Part1.GPIO58, R1.Pin_1
  N5: R1.Pin_0, LED1.anode
  N6: R2.Pin_0, LED2.anode
  N7: R3.Pin_0, LED3.anode
